# Fritzing sketch sim_project (saved by Fritzing 1.0.5)
breadboards: 1

parts:
  Part1 = Current Sensor 5A
  OLED1 = 128x32 I2C Monochrome OLED Display
  Part2 = Arduino Wireless SD Shield
  Part3 = Arduino Uno (Rev3)
  R1 = Resistor [tolerance=±5% resistance=220 package="2512 [SMD]"]

nets:
  N1: Part1.VCC, R1.Pin_0
  GND: Part1.GND, OLED1.GND, Part2.GND, Part3.GND
  N2: OLED1.SDA, Part2.A4, Part3.A4/SDA
  N3: OLED1.SCL, Part2.A5, Part3.A5/SCL
  3.3V: OLED1.3.3V, Part2.+5V, Part3.5V
  N4: Part2.A0, Part3.A0, R1.Pin_1
  N5: Part2.D8, Part3.D8
  N6: Part2.D9, Part3.D9_PWM
  N7: Part2.D10, Part3.D10_PWM/SS
  N8: Part2.D11, Part3.D11_PWM/MOSI
  N9: Part2.D12, Part3.D12/MISO
  N10: Part2.D13, Part3.D13/SCK
  N11: Part2.AREF, Part3.AREF
  N12: Part2.A1, Part3.A1
  N13: Part2.A2, Part3.A2
  N14: Part2.A3, Part3.A3
  N15: Part2.ARDUINO-RX(0), Part3.D0/RX
  N16: Part2.ARDUINO-TX(1), Part3.D1/TX
  N17: Part2.D2, Part3.D2
  N18: Part2.D3, Part3.D3_PWM
  N19: Part2.SD_CS, Part3.D4
  N20: Part2.D5, Part3.D5_PWM
  N21: Part2.D6, Part3.D6_PWM
  N22: Part2.D7, Part3.D7
  3.3V_2: Part2.3.3V, Part3.3V3
  N23: Part2.RESET, Part3.RESET
  VIN: Part2.VIN, Part3.VIN
